# Fritzing sketch sketch (saved by Fritzing 0.9.3b)
breadboards: 1

parts:
  Composant1 = Arduino Uno (Rev3) - ICSP
  IC1 = L293D [package=THT]
  M1 = DC Motor
  M2 = DC Motor
  VCC1 = 4 x AAA Battery Mount
  S1 = Pushbutton [package="[THT]"]
  R1 = Resistor [tolerance=±5% resistance=100 package="0805 [SMD]"]
  J1 = Basic Servo
  S2 = Pushbutton [package="[THT]"]
  R2 = Resistor [tolerance=±5% resistance=100 package="0805 [SMD]"]
  M3 = DC Motor
  Q1 = NPN-Transistor [package="TO92 [THT]"]
  hc-sr1 = hc-sr04

nets:
  N1: Composant1.ICSP_MISO, Composant1.D12/MISO, hc-sr1.Trig
  VCC: Composant1.5V, IC1.+Vmotor, IC1.+V, VCC1.+, S1.Pin_3, S1.Pin_4, J1.vcc, S2.Pin_3, S2.Pin_4, M3.pin_1, hc-sr1.VCC
  N2: Composant1.D8, Q1.B
  N3: Composant1.D9_PWM, J1.pulse
  N4: Composant1.D10_PWM/SS, IC1.Enable_1
  N5: Composant1.D11_PWM/MOSI, IC1.Enable_2
  N6: Composant1.D13/SCK, hc-sr1.Echo
  N7: Composant1.D2, S1.Pin_1, S1.Pin_2
  N8: Composant1.D3_PWM, S2.Pin_1, S2.Pin_2
  N9: Composant1.D4, IC1.In_2
  N10: Composant1.D5_PWM, IC1.In_1
  N11: Composant1.D6_PWM, IC1.In_3
  N12: Composant1.D7, IC1.In_4
  GND: Composant1.GND, IC1.0V, VCC1.-, R1.Pin_1, J1.gnd, R2.Pin_1, Q1.C, hc-sr1.GND
  N13: IC1.Out_1_(_Controlled_by_Enable_1_), M1.pin_1
  N14: IC1.Out_2_(_Controlled_by_Enable_1_), M1.pin_2
  N15: IC1.Out_3_(_Controlled_by_Enable_2_), M2.pin_2
  N16: IC1.Out_4_(_Controlled_by_Enable_2_), M2.pin_1
  N17: M3.pin_2, Q1.E
